// Logisim project cpu.circ as structural Verilog: 4 circuits, main circuit main
module main (
  input  in_1
);

  wire adder_1_cout, alu_1_flag, and_1_out, button_1_out, clock_1_out, decoder_1_j,
       decoder_1_jmp_if_flag_or_j, decoder_1_low_jmp_ram__high_jmp_input, decoder_1_low_ram__high_input,
       decoder_1_low_ram_in__high_ram_reg, decoder_1_write_ra, decoder_1_write_ram, decoder_1_write_ram_reg,
       decoder_1_write_rb, not_1_out, or_1_out, register_5_q;
  wire [3:0] rom_1_data, rom_1_data_3;
  wire [15:0] adder_1_out, alu_1_output, controlled_buffer_1_out, mux_16_1_output, mux_16_2_output,
       mux_16_3_output, mux_16_4_output, mux_16_5_output, ram_1_data, register_1_q, register_2_q,
       register_3_q, register_4_q, rom_1_data_2;

  not not_1 (not_1_out, adder_1_cout);
  Clock clock_1 (.out(clock_1_out));
  Button button_1 (.out(button_1_out));
  Adder #(.width(16)) adder_1 (.a(register_1_q), .b(16'h1), .out(adder_1_out), .cout(adder_1_cout));  // open: cin
  mux_16 mux_16_1 (
    .Input_A(adder_1_out), .Input_B(controlled_buffer_1_out), .Output(mux_16_1_output),
    .Select(decoder_1_jmp_if_flag_or_j));
  and and_1 (and_1_out, not_1_out, clock_1_out, in_1);
  Register #(.width(16), .trigger("falling")) register_1 (
    .D(mux_16_1_output), .Q(register_1_q), .clk(and_1_out), .clr(button_1_out));  // open: en
  decoder decoder_1 (
    .Low_RAM__High_INPUT(decoder_1_low_ram__high_input), .Write_RAM_REG(decoder_1_write_ram_reg),
    .Write_RA(decoder_1_write_ra), .Write_RB(decoder_1_write_rb), .Write_RAM(decoder_1_write_ram),
    .in_1(rom_1_data_3), .Low_RAM_IN__High_RAM_REG(decoder_1_low_ram_in__high_ram_reg),
    .Low_JMP_RAM__High_JMP_INPUT(decoder_1_low_jmp_ram__high_jmp_input),
    .JMP_if_FLAG_or_J(decoder_1_jmp_if_flag_or_j), .Enable(and_1_out), .J(decoder_1_j));
  mux_16 mux_16_2 (
    .Input_A(ram_1_data), .Input_B(rom_1_data_2), .Output(mux_16_2_output),
    .Select(decoder_1_low_jmp_ram__high_jmp_input));
  assign controlled_buffer_1_out = or_1_out ? mux_16_2_output : 16'bz;  // Controlled_Buffer controlled_buffer_1
  ROM #(.addrWidth(16), .dataWidth(24)) rom_1 (
    .addr(register_1_q), .data({rom_1_data_3, rom_1_data, rom_1_data_2}));  // open: sel
  mux_16 mux_16_3 (
    .Input_A(ram_1_data), .Input_B(rom_1_data_2), .Output(mux_16_3_output),
    .Select(decoder_1_low_ram__high_input));
  mux_16 mux_16_4 (
    .Input_A(ram_1_data), .Input_B(rom_1_data_2), .Output(mux_16_4_output),
    .Select(decoder_1_low_ram__high_input));
  or or_1 (or_1_out, register_5_q, decoder_1_j);
  Register #(.width(16), .trigger("falling")) register_2 (
    .D(mux_16_3_output), .Q(register_2_q), .clk(decoder_1_write_ra), .clr(button_1_out));  // open: en
  Register #(.width(16), .trigger("falling")) register_3 (
    .D(mux_16_4_output), .Q(register_3_q), .clk(decoder_1_write_rb), .clr(button_1_out));  // open: en
  Register #(.width(16), .trigger("falling")) register_4 (
    .D(ram_1_data), .Q(register_4_q), .clk(decoder_1_write_ram_reg), .clr(button_1_out));  // open: en
  mux_16 mux_16_5 (
    .Input_A(rom_1_data_2), .Input_B(register_4_q), .Output(mux_16_5_output),
    .Select(decoder_1_low_ram_in__high_ram_reg));
  alu alu_1 (
    .Input_A(register_2_q), .Input_B(register_3_q), .Output(alu_1_output), .Operation(rom_1_data),
    .Flag(alu_1_flag));
  Register #(.width(1)) register_5 (
    .D(alu_1_flag), .Q(register_5_q), .clk(decoder_1_write_ram), .clr(button_1_out));  // open: en
  RAM #(.addrWidth(16), .dataWidth(16), .bus("separate")) ram_1 (
    .addr(mux_16_5_output), .din(alu_1_output), .data(ram_1_data), .clk(decoder_1_write_ram),
    .clr(button_1_out));  // open: str, sel, ld
endmodule

module alu (
  input  [15:0] Input_A,
  input  [15:0] Input_B,
  input  [3:0] Operation,
  output Flag,
  output [15:0] Output
);

  wire comparator_1_eq, comparator_1_gt, comparator_1_lt, decoder_1_out1, decoder_1_out2, decoder_1_out3,
       decoder_1_out4, decoder_1_out5, decoder_1_out6, decoder_1_out7, decoder_1_out8, decoder_1_out9,
       decoder_1_out10, decoder_1_out11, decoder_1_out12, decoder_1_out13, decoder_1_out14, decoder_1_out15,
       nor_1_out, nor_2_out, not_1_out;
  wire [15:0] adder_1_out, and_1_out, divider_1_out, divider_1_rem, multiplier_1_out, not_2_out, or_1_out,
       shifter_1_out, shifter_2_out, subtractor_1_out, xor_1_out;

  Comparator #(.width(16)) comparator_1 (
    .a(Input_A), .b(Input_B), .gt(comparator_1_gt), .eq(comparator_1_eq), .lt(comparator_1_lt));
  not not_1 (not_1_out, comparator_1_eq);
  assign Output = decoder_1_out5 ? not_2_out : 16'bz;  // Controlled_Buffer controlled_buffer_1
  assign not_2_out = ~Input_A;  // NOT_Gate not_2, 16 bits wide
  Adder #(.width(16)) adder_1 (.a(Input_A), .b(Input_B), .out(adder_1_out));  // open: cin, cout
  assign Output = decoder_1_out6 ? adder_1_out : 16'bz;  // Controlled_Buffer controlled_buffer_2
  Subtractor #(.width(16)) subtractor_1 (.a(Input_A), .b(Input_B), .out(subtractor_1_out));  // open: bin, bout
  assign Output = decoder_1_out7 ? subtractor_1_out : 16'bz;  // Controlled_Buffer controlled_buffer_3
  Multiplier #(.width(16)) multiplier_1 (.a(Input_A), .b(Input_B), .out(multiplier_1_out));  // open: cin, cout
  assign Output = decoder_1_out8 ? multiplier_1_out : 16'bz;  // Controlled_Buffer controlled_buffer_4
  Divider #(.width(16)) divider_1 (.a(Input_A), .b(Input_B), .out(divider_1_out), .rem(divider_1_rem));  // open: upper
  assign Output = decoder_1_out9 ? divider_1_out : 16'bz;  // Controlled_Buffer controlled_buffer_5
  assign Output = decoder_1_out10 ? divider_1_rem : 16'bz;  // Controlled_Buffer controlled_buffer_6
  Shifter #(.width(16)) shifter_1 (.in(Input_A), .\dist (Input_B[3:0]), .out(shifter_1_out));
  assign Output = decoder_1_out11 ? shifter_1_out : 16'bz;  // Controlled_Buffer controlled_buffer_7
  Shifter #(.width(16), .shift("lr")) shifter_2 (.in(Input_A), .\dist (Input_B[3:0]), .out(shifter_2_out));
  assign Output = decoder_1_out12 ? shifter_2_out : 16'bz;  // Controlled_Buffer controlled_buffer_8
  assign xor_1_out = Input_A ^ Input_B;  // XOR_Gate xor_1, 16 bits wide
  assign Output = decoder_1_out13 ? xor_1_out : 16'bz;  // Controlled_Buffer controlled_buffer_9
  assign Output = decoder_1_out14 ? and_1_out : 16'bz;  // Controlled_Buffer controlled_buffer_10
  assign and_1_out = Input_A & Input_B;  // AND_Gate and_1, 16 bits wide
  assign or_1_out = Input_A | Input_B;  // OR_Gate or_1, 16 bits wide
  assign Output = decoder_1_out15 ? or_1_out : 16'bz;  // Controlled_Buffer controlled_buffer_11
  assign Flag = nor_1_out ? 1'b0 : 1'bz;  // Controlled_Buffer controlled_buffer_12
  nor nor_1 (nor_1_out, decoder_1_out1, decoder_1_out2, decoder_1_out3, decoder_1_out4);
  assign Flag = decoder_1_out1 ? comparator_1_gt : 1'bz;  // Controlled_Buffer controlled_buffer_13
  assign Flag = decoder_1_out2 ? comparator_1_eq : 1'bz;  // Controlled_Buffer controlled_buffer_14
  assign Flag = decoder_1_out3 ? comparator_1_lt : 1'bz;  // Controlled_Buffer controlled_buffer_15
  assign Flag = decoder_1_out4 ? not_1_out : 1'bz;  // Controlled_Buffer controlled_buffer_16
  assign Output = nor_2_out ? {16{1'b0}} : 16'bz;  // Controlled_Buffer controlled_buffer_17
  nor nor_2 (nor_2_out, decoder_1_out5, decoder_1_out6, decoder_1_out7, decoder_1_out8, decoder_1_out9, decoder_1_out10, decoder_1_out11, decoder_1_out12, decoder_1_out13, decoder_1_out14, decoder_1_out15);
  Decoder #(.select(4)) decoder_1 (
    .out1(decoder_1_out1), .out2(decoder_1_out2), .out3(decoder_1_out3), .out4(decoder_1_out4),
    .out5(decoder_1_out5), .out6(decoder_1_out6), .out7(decoder_1_out7), .out8(decoder_1_out8),
    .out9(decoder_1_out9), .out10(decoder_1_out10), .out11(decoder_1_out11), .out12(decoder_1_out12),
    .out13(decoder_1_out13), .out14(decoder_1_out14), .out15(decoder_1_out15), .sel(Operation));  // open: out0, en
endmodule

module mux_16 (
  input  [15:0] Input_A,
  input  [15:0] Input_B,
  input  Select,
  output [15:0] Output
);

  wire not_1_out;

  not not_1 (not_1_out, Select);
  assign Output = not_1_out ? Input_A : 16'bz;  // Controlled_Buffer controlled_buffer_1
  assign Output = Select ? Input_B : 16'bz;  // Controlled_Buffer controlled_buffer_2
endmodule

module decoder (
  input  [3:0] in_1,
  input  Enable,
  output Low_RAM_IN__High_RAM_REG,
  output Write_RAM_REG,
  output Low_RAM__High_INPUT,
  output Write_RA,
  output Write_RB,
  output Write_RAM,
  output Low_JMP_RAM__High_JMP_INPUT,
  output JMP_if_FLAG_or_J,
  output J
);

  wire decoder_1_out1, decoder_1_out2, decoder_1_out3, decoder_1_out4, decoder_1_out5, decoder_1_out6,
       decoder_1_out7, decoder_1_out8, decoder_1_out9, decoder_1_out10, decoder_1_out11, decoder_1_out12,
       decoder_1_out13, decoder_1_out14, decoder_1_out15;

  Decoder #(.select(4), .disabled(0)) decoder_1 (
    .out1(decoder_1_out1), .out2(decoder_1_out2), .out3(decoder_1_out3), .out4(decoder_1_out4),
    .out5(decoder_1_out5), .out6(decoder_1_out6), .out7(decoder_1_out7), .out8(decoder_1_out8),
    .out9(decoder_1_out9), .out10(decoder_1_out10), .out11(decoder_1_out11), .out12(decoder_1_out12),
    .out13(decoder_1_out13), .out14(decoder_1_out14), .out15(decoder_1_out15), .sel(in_1), .en(Enable));  // open: out0
  or or_1 (Low_RAM_IN__High_RAM_REG, decoder_1_out13, decoder_1_out5, decoder_1_out6, decoder_1_out8, decoder_1_out10);
  or or_2 (Write_RAM_REG, decoder_1_out7, decoder_1_out8);
  or or_3 (Low_RAM__High_INPUT, decoder_1_out1, decoder_1_out2);
  or or_4 (Write_RA, decoder_1_out1, decoder_1_out3, decoder_1_out5);
  or or_5 (Write_RB, decoder_1_out2, decoder_1_out4, decoder_1_out6);
  or or_6 (Write_RAM, decoder_1_out9, decoder_1_out10);
  or or_7 (Low_JMP_RAM__High_JMP_INPUT, decoder_1_out14, decoder_1_out11);
  or or_8 (JMP_if_FLAG_or_J, decoder_1_out14, decoder_1_out11, decoder_1_out12, decoder_1_out13, decoder_1_out15);
  or or_9 (J, decoder_1_out14, decoder_1_out15);
endmodule
